# Fritzing sketch Arduino Shield (saved by Fritzing 0.8.7b)
circuit board: 9.52558cm x 5.81941cm
breadboards: 1

parts:
  LED1 = RGB LED (com. cathode, rbg) [package="5 mm [THT]"]
  R1 = Resistor [tolerance=±5% resistance=220 package=THT]
  R2 = Resistor [tolerance=±5% resistance=220 package=THT]
  R3 = Resistor [tolerance=±5% resistance=220 package=THT]
  LED2 = RGB LED (com. cathode, rbg) [package="5 mm [THT]"]
  R4 = Resistor [tolerance=±5% resistance=220 package=THT]
  R5 = Resistor [tolerance=±5% resistance=220 package=THT]
  R6 = Resistor [tolerance=±5% resistance=220 package=THT]
  J2 = molex pin header, 4 pins [form=molex]
  J3 = molex pin header, 4 pins [form=molex]
  J4 = molex pin header, 4 pins [form=molex]
  J5 = molex pin header, 4 pins [form=molex]
  J6 = molex pin header, 4 pins [form=molex]
  Power_plug1 = Power plug
  U1 = RF-LINK_RX [package=rf-link_rx]
  ANT1 = Antenna
  J1 = molex pin header, 4 pins [form=molex]
  Part1 = Arduino Mega 2560 (Rev3)

nets:
  N1: LED1.red_anode, R1.Pin_1
  +5V: LED1.common_cathode, LED2.common_cathode, J6.pin1, U1.+5V, Part1.5V
  N2: LED1.blue_anode, R2.Pin_1
  N3: LED1.green_anode, R3.Pin_1
  N4: R1.Pin_0, Part1.D13_PWM
  N5: R2.Pin_0, Part1.D12_PWM
  N6: R3.Pin_0, Part1.D11_PWM
  N7: LED2.red_anode, R4.Pin_1
  N8: LED2.blue_anode, R5.Pin_1
  N9: LED2.green_anode, R6.Pin_1
  N10: R4.Pin_0, Part1.D10_PWM
  N11: R5.Pin_0, Part1.D9_PWM
  N12: R6.Pin_0, Part1.D8_PWM
  N13: J2.pin1, Part1.D22
  N14: J2.pin2, Part1.D24
  N15: J2.pin3, Part1.D26
  N16: J2.pin4, Part1.D28
  N17: J3.pin1, Part1.D30
  N18: J3.pin2, Part1.D32
  N19: J3.pin3, Part1.D33, Part1.D35, Part1.D36
  N20: J3.pin4, Part1.D34
  N21: J4.pin1, Part1.D40
  N22: J4.pin2, Part1.D38, Part1.D41
  N23: J4.pin3, Part1.D42
  N24: J4.pin4, Part1.D44
  N25: J5.pin1, Part1.D46
  N26: J5.pin2, Part1.D48
  N27: J5.pin3, Part1.D50
  N28: J5.pin4, Part1.D52
  GND: J6.pin2, J6.pin3, Power_plug1.GND, U1.GND, Part1.GND
  VCC: J6.pin4, Power_plug1.VCC, Part1.VIN
  N29: U1.DATA, Part1.D2_PWM
  N30: U1.ANT, ANT1.antenna_lead
  N31: J1.pin1, Part1.D6_PWM
  N32: J1.pin2, Part1.D5_PWM
  N33: J1.pin3, Part1.D4_PWM
  N34: J1.pin4, Part1.D3_PWM

notes:
  Pan/Tilt &
  Cable Cam
  v1.0 Feb 3 2014
  Alex Forey
  CC-BY-NC-SA
  PWM
