# Fritzing sketch Motor Board (saved by Fritzing 0.8.7b)
circuit board: 9.2019cm x 13.3353cm
breadboards: 1

parts:
  IC4 = L293D [package=THT]
  IC5 = L293D [package=THT]
  M5 = Stepper Motor - Bipolar
  IC6 = L293D [package=THT]
  M6 = Stepper Motor - Bipolar
  IC7 = L293D [package=THT]
  M7 = Stepper Motor - Bipolar
  IC8 = L293D [package=THT]
  M8 = Stepper Motor - Bipolar
  J2 = molex pin header, 4 pins [form=molex]
  J4 = molex pin header, 4 pins [form=molex]
  J7 = molex pin header, 4 pins [form=molex]
  J8 = molex pin header, 4 pins [form=molex]
  J6 = molex pin header, 4 pins [form=molex]
  J9 = molex pin header, 4 pins [form=molex]
  J10 = molex pin header, 4 pins [form=molex]

nets (from the pcb view):
  N1: IC4.Enable_1, IC4.+Vmotor, IC4.Enable_2, IC4.+V, IC5.Enable_1, IC5.+Vmotor, IC5.Enable_2, IC5.+V, IC6.Enable_1, IC6.+Vmotor, IC6.Enable_2, IC6.+V, IC7.Enable_1, IC7.+Vmotor, IC7.Enable_2, IC7.+V, IC8.Enable_1, IC8.+Vmotor, IC8.Enable_2, IC8.+V, J2.pin4
  N2: IC4.In_1, J10.pin1
  N3: IC4.Out_1_(_Controlled_by_Enable_1_), J4.pin1
  N4: IC4.0V, IC5.0V, IC6.0V, IC7.0V, IC8.0V, J2.pin3
  N5: IC4.Out_2_(_Controlled_by_Enable_1_), J4.pin2
  N6: IC4.In_2, J10.pin2
  N7: IC4.In_3, J10.pin4
  N8: IC4.Out_3_(_Controlled_by_Enable_2_), J4.pin4
  N9: IC4.Out_4_(_Controlled_by_Enable_2_), J4.pin3
  N10: IC4.In_4, J10.pin3
  N11: IC5.In_1, M5.A
  N12: IC5.Out_1_(_Controlled_by_Enable_1_), J6.pin1
  N13: IC5.Out_2_(_Controlled_by_Enable_1_), J6.pin2
  N14: IC5.In_2, M5.C
  N15: IC5.In_3, M5.D
  N16: IC5.Out_3_(_Controlled_by_Enable_2_), J6.pin4
  N17: IC5.Out_4_(_Controlled_by_Enable_2_), J6.pin3
  N18: IC5.In_4, M5.B
  N19: IC6.In_1, M6.A
  N20: IC6.Out_1_(_Controlled_by_Enable_1_), J7.pin1
  N21: IC6.Out_2_(_Controlled_by_Enable_1_), J7.pin2
  N22: IC6.In_2, M6.C
  N23: IC6.In_3, M6.D
  N24: IC6.Out_3_(_Controlled_by_Enable_2_), J7.pin4
  N25: IC6.Out_4_(_Controlled_by_Enable_2_), J7.pin3
  N26: IC6.In_4, M6.B
  N27: IC7.In_1, M7.A
  N28: IC7.Out_1_(_Controlled_by_Enable_1_), J8.pin1
  N29: IC7.Out_2_(_Controlled_by_Enable_1_), J8.pin2
  N30: IC7.In_2, M7.C
  N31: IC7.In_3, M7.D
  N32: IC7.Out_3_(_Controlled_by_Enable_2_), J8.pin4
  N33: IC7.Out_4_(_Controlled_by_Enable_2_), J8.pin3
  N34: IC7.In_4, M7.B
  N35: IC8.In_1, M8.A
  N36: IC8.Out_1_(_Controlled_by_Enable_1_), J9.pin1
  N37: IC8.Out_2_(_Controlled_by_Enable_1_), J9.pin2
  N38: IC8.In_2, M8.C
  N39: IC8.In_3, M8.D
  N40: IC8.Out_3_(_Controlled_by_Enable_2_), J9.pin4
  N41: IC8.Out_4_(_Controlled_by_Enable_2_), J9.pin3
  N42: IC8.In_4, M8.B

notes:
  Pan
  A/B/C/D
  Tilt
  Roll
  Linear Stepper
  Linear PWM
  D/C/B/A
  Pan/Tilt &
  Cable Cam
  Motor Board
  v1.0
  3 Feb 2014
  Alex Forey
  CC-By-NC-SA
